# Fritzing sketch binary_counter (saved by Fritzing 0.9.3b)
breadboards: 1

parts:
  Part1 = Arduino Mega 2560 (Rev3)
  R1 = Resistor [tolerance=±5% resistance=1k package=THT]
  R2 = Resistor [tolerance=±5% resistance=1k package=THT]
  R3 = Resistor [tolerance=±5% resistance=1k package=THT]
  R4 = Resistor [tolerance=±5% resistance=1k package=THT]
  R5 = Resistor [tolerance=±5% resistance=1k package=THT]
  LED1 = LED - 3mm [color="Red (633nm)" package="3 mm [THT]"]
  LED2 = LED - 3mm [color="Orange (620nm)" package="3 mm [THT]"]
  LED3 = LED - 3mm [color="Green (555nm)" package="3 mm [THT]"]
  LED4 = LED - 3mm [color="Blue (430nm)" package="3 mm [THT]"]
  LED5 = LED - 3mm [color="Yellow (595nm)" package="3 mm [THT]"]
  R6 = Resistor [tolerance=±5% resistance=10k package=THT]
  S1 = Pushbutton [package="[THT]"]

nets:
  N1: Part1.5V, S1.Pin_3, S1.Pin_4
  N2: Part1.GND, LED1.cathode, LED2.cathode, LED3.cathode, LED4.cathode, LED5.cathode, R6.Pin_1
  N3: Part1.D2_PWM, R6.Pin_0, S1.Pin_1, S1.Pin_2
  N4: Part1.D44, R5.Pin_0
  N5: Part1.D46, R4.Pin_0
  N6: Part1.D48, R3.Pin_0
  N7: Part1.D50, R2.Pin_0
  N8: Part1.D52, R1.Pin_0
  N9: R1.Pin_1, LED1.anode
  N10: R2.Pin_1, LED2.anode
  N11: R3.Pin_1, LED3.anode
  N12: R4.Pin_1, LED4.anode
  N13: R5.Pin_1, LED5.anode
