# Fritzing sketch binary_counter_nano (saved by Fritzing 0.9.6b)
breadboards: 1

parts:
  R1 = Resistor [tolerance=±5% resistance=1k power=0.25 package=THT]
  R2 = Resistor [tolerance=±5% resistance=1k power=0.25 package=THT]
  R3 = Resistor [tolerance=±5% resistance=1k power=0.25 package=THT]
  R4 = Resistor [tolerance=±5% resistance=1k power=0.25 package=THT]
  R5 = Resistor [tolerance=±5% resistance=1k power=0.25 package=THT]
  LED1 = LED - 3mm [color="Red (633nm)" current=0.030 package="3 mm [THT]"]
  LED2 = LED - 3mm [color="Orange (620nm)" current=0.030 package="3 mm [THT]"]
  LED3 = LED - 3mm [color="Green (555nm)" current=0.030 package="3 mm [THT]"]
  LED4 = LED - 3mm [color="Blue (430nm)" current=0.030 package="3 mm [THT]"]
  LED5 = LED - 3mm [color="Yellow (595nm)" current=0.030 package="3 mm [THT]"]
  R6 = Resistor [tolerance=±5% resistance=10k power=0.25 package=THT]
  S1 = Pushbutton [package="[THT]"]
  Part2 = Arduino Nano (Rev3.0)

nets:
  N1: R1.Pin_0, Part2.D3
  N2: R1.Pin_1, LED1.anode
  N3: R2.Pin_0, Part2.D4
  N4: R2.Pin_1, LED2.anode
  N5: R3.Pin_0, Part2.D5
  N6: R3.Pin_1, LED3.anode
  N7: R4.Pin_0, Part2.D6
  N8: R4.Pin_1, LED4.anode
  N9: R5.Pin_0, Part2.D7
  N10: R5.Pin_1, LED5.anode
  N11: LED1.cathode, LED2.cathode, LED3.cathode, LED4.cathode, LED5.cathode, R6.Pin_1, Part2.GND
  N12: R6.Pin_0, S1.Pin_1, S1.Pin_2, Part2.D2
  N13: S1.Pin_3, S1.Pin_4, Part2.5V
