# Fritzing sketch blink_attiny (saved by Fritzing 0.9.6b)
breadboards: 1

parts:
  U1 = attiny85 [package=dip]
  LED1 = LED - 5mm [color="Green (565nm)" current=0.030 package="5 mm [THT]"]
  R1 = Resistor [tolerance=±5% resistance=1k package="1206 [SMD]"]
  VCC1 = 4 x AAA Battery Mount

nets:
  N1: U1.Pin_3, LED1.anode
  N2: U1.Pin_4, R1.Pin_1, VCC1.-
  N3: U1.Pin_8, VCC1.+
  N4: LED1.cathode, R1.Pin_0
